// Logisim project RAM.circ as structural Verilog: 1 circuit, main circuit RAM
module RAM (
  input  [9:0] ADDR,
  input  [31:0] in_2,
  input  in_3,
  input  in_4,
  input  [31:0] in_5,
  input  in_6,
  input  in_7,
  input  in_8,
  input  in_9,
  input  [31:0] in_10,
  input  [31:0] in_11,
  input  [31:0] in_12,
  input  [31:0] in_13,
  input  in_14,
  input  in_15,
  input  in_16,
  input  [31:0] in_17,
  input  in_18,
  input  in_19,
  input  [31:0] in_20,
  input  [31:0] in_21,
  input  [31:0] in_22,
  input  [31:0] in_23,
  input  in_24,
  input  in_25,
  input  [31:0] in_26,
  input  in_27,
  input  in_28,
  input  in_29,
  input  [31:0] in_30,
  input  [31:0] in_31,
  input  [31:0] in_32,
  input  [31:0] in_33,
  input  in_34,
  input  in_35,
  input  in_36,
  input  in_37,
  input  in_38,
  input  [31:0] in_39,
  input  [31:0] in_40,
  input  [31:0] in_41,
  input  [31:0] in_42,
  output [31:0] out_43,
  output [31:0] out_44,
  output [31:0] out_45,
  output [31:0] out_46,
  output [31:0] out_47,
  output [31:0] out_48,
  output [31:0] out_49,
  output [31:0] out_50,
  output [31:0] out_51,
  output [31:0] out_52,
  output [31:0] out_53,
  output [31:0] out_54,
  output [31:0] out_55,
  output [31:0] out_56,
  output [31:0] out_57,
  output [31:0] out_58,
  output [31:0] out_59,
  output [31:0] out_60,
  output [31:0] out_61,
  output [31:0] out_62
);

  RAM_part #(.addrWidth(10), .dataWidth(32), .bus("separate"), .Select("high")) _0 (
    .addr(ADDR), .din(in_2), .data(out_43), .str(in_4), .clk(in_3));  // open: sel, ld, clr
  RAM_part #(.addrWidth(10), .dataWidth(32), .bus("separate"), .Select("high")) _5 (
    .addr(ADDR), .din(in_13), .data(out_48), .str(in_14), .clk(in_3));  // open: sel, ld, clr
  RAM_part #(.addrWidth(10), .dataWidth(32), .bus("separate"), .Select("high")) _10 (
    .addr(ADDR), .din(in_23), .data(out_53), .str(in_24), .clk(in_3));  // open: sel, ld, clr
  RAM_part #(.addrWidth(10), .dataWidth(32), .bus("separate"), .Select("high")) _15 (
    .addr(ADDR), .din(in_33), .data(out_58), .str(in_34), .clk(in_3));  // open: sel, ld, clr
  RAM_part #(.addrWidth(10), .dataWidth(32), .bus("separate"), .Select("high")) _1 (
    .addr(ADDR), .din(in_5), .data(out_44), .str(in_6), .clk(in_3));  // open: sel, ld, clr
  RAM_part #(.addrWidth(10), .dataWidth(32), .bus("separate"), .Select("high")) _6 (
    .addr(ADDR), .din(in_17), .data(out_49), .str(in_15), .clk(in_3));  // open: sel, ld, clr
  RAM_part #(.addrWidth(10), .dataWidth(32), .bus("separate"), .Select("high")) _11 (
    .addr(ADDR), .din(in_26), .data(out_54), .str(in_25), .clk(in_3));  // open: sel, ld, clr
  RAM_part #(.addrWidth(10), .dataWidth(32), .bus("separate"), .Select("high")) _16 (
    .addr(ADDR), .din(in_39), .data(out_59), .str(in_35), .clk(in_3));  // open: sel, ld, clr
  RAM_part #(.addrWidth(10), .dataWidth(32), .bus("separate"), .Select("high")) _2 (
    .addr(ADDR), .din(in_10), .data(out_45), .str(in_7), .clk(in_3));  // open: sel, ld, clr
  RAM_part #(.addrWidth(10), .dataWidth(32), .bus("separate"), .Select("high")) _7 (
    .addr(ADDR), .din(in_20), .data(out_50), .str(in_16), .clk(in_3));  // open: sel, ld, clr
  RAM_part #(.addrWidth(10), .dataWidth(32), .bus("separate"), .Select("high")) _12 (
    .addr(ADDR), .din(in_30), .data(out_55), .str(in_27), .clk(in_3));  // open: sel, ld, clr
  RAM_part #(.addrWidth(10), .dataWidth(32), .bus("separate"), .Select("high")) _17 (
    .addr(ADDR), .din(in_40), .data(out_60), .str(in_36), .clk(in_3));  // open: sel, ld, clr
  RAM_part #(.addrWidth(10), .dataWidth(32), .bus("separate"), .Select("high")) _3 (
    .addr(ADDR), .din(in_11), .data(out_46), .str(in_8), .clk(in_3));  // open: sel, ld, clr
  RAM_part #(.addrWidth(10), .dataWidth(32), .bus("separate"), .Select("high")) _8 (
    .addr(ADDR), .din(in_21), .data(out_51), .str(in_18), .clk(in_3));  // open: sel, ld, clr
  RAM_part #(.addrWidth(10), .dataWidth(32), .bus("separate"), .Select("high")) _13 (
    .addr(ADDR), .din(in_31), .data(out_56), .str(in_28), .clk(in_3));  // open: sel, ld, clr
  RAM_part #(.addrWidth(10), .dataWidth(32), .bus("separate"), .Select("high")) _18 (
    .addr(ADDR), .din(in_41), .data(out_61), .str(in_37), .clk(in_3));  // open: sel, ld, clr
  RAM_part #(.addrWidth(10), .dataWidth(32), .bus("separate"), .Select("high")) _4 (
    .addr(ADDR), .din(in_12), .data(out_47), .str(in_9), .clk(in_3));  // open: sel, ld, clr
  RAM_part #(.addrWidth(10), .dataWidth(32), .bus("separate"), .Select("high")) _9 (
    .addr(ADDR), .din(in_22), .data(out_52), .str(in_19), .clk(in_3));  // open: sel, ld, clr
  RAM_part #(.addrWidth(10), .dataWidth(32), .bus("separate"), .Select("high")) _14 (
    .addr(ADDR), .din(in_32), .data(out_57), .str(in_29), .clk(in_3));  // open: sel, ld, clr
  RAM_part #(.addrWidth(10), .dataWidth(32), .bus("separate"), .Select("high")) _19 (
    .addr(ADDR), .din(in_42), .data(out_62), .str(in_38), .clk(in_3));  // open: sel, ld, clr
endmodule
